# Fritzing sketch msft (saved by Fritzing 0.9.10b)
breadboards: 1

parts:
  U1 = LIPO-2000mAh [package=lipo-2000]
  Part2 = USB LiPoly Charger
  Part3 = LED Tactile Button Breakout v10 [part_number=BOB-10467]
  Mod2 = Heltec WiFi LoRa 32 V2 [part_number=HTIT-WB32LA]
  R1 = Resistor [tolerance=±5% resistance=1000 package="2512 [SMD]"]

nets:
  N1: U1.+, Part2.VBAT, Mod2.pin_20
  GND: U1.-, Part2.GND, Part3.4, Mod2.GND
  N2: Part3.1, Part3.3, Mod2.pin_33
  N3: Part3.2, R1.Pin_0
  N4: Mod2.pin_16, Mod2.pin_17, R1.Pin_1
  N5: Mod2.pin_21, Mod2.pin_22
